# Fritzing sketch Working Circuit (saved by Fritzing 0.9.3b)
breadboards: 1

parts:
  Conveyance_Arduino = Arduino Mega 2560 (Rev3)
  Sorting_Arduino = Arduino Mega 2560 (Rev3)
  Raspberry_Pi_1 = Raspberry Pi 3 [part_number=RPI-3-V1.2]  # not connected
  Good_Servo_Arm = Dagu DGServo 9g (Pan and tilt) [part_number=RS001B]
  Good_Proxy = fc-51 [package=THT]
  Vision_Detection_Proxy = fc-51 [package=THT]
  BAT1 = BC9VPC [package=bc9vpc]
  Conveyor_Motor = DC Motor
  Part3 = HX711 Weighing Sensor Module
  Load_Cell_(1kg)_-_Good = Load Cell - Red/white/black/green
  SERIAL_COMM_2 = USB A Plug
  SERIAL_COMM_1 = USB A Plug
  USBTTL3 = Micro USB B Plug
  USBTTL4 = Micro USB B Plug
  Buffer_Motor = DC Motor
  L298N1 = L298N DC motor driver
  Part4 = HX711 Weighing Sensor Module
  Load_Cell_(1kg)_-_Bad = Load Cell - Red/white/black/green
  Part5 = HX711 Weighing Sensor Module
  Load_Cell_(1kg)_Defected = Load Cell - Red/white/black/green
  Bad_Servo_Arm = Dagu DGServo 9g (Pan and tilt) [part_number=RS001B]
  Bad_Proxy = fc-51 [package=THT]
  Defected_Servo_Arm = Dagu DGServo 9g (Pan and tilt) [part_number=RS001B]
  Defected_Proxy = fc-51 [package=THT]

nets:
  N1: Conveyance_Arduino.D9_PWM, Vision_Detection_Proxy.pin1
  N2: Conveyance_Arduino.5V, Vision_Detection_Proxy.pin3
  GND: Conveyance_Arduino.GND, Vision_Detection_Proxy.pin2, BAT1.V-, L298N1.GND
  N3: Conveyance_Arduino.D4_PWM, L298N1.IN4
  N4: Conveyance_Arduino.D5_PWM, L298N1.IN3
  N5: Conveyance_Arduino.D6_PWM, L298N1.IN2
  N6: Conveyance_Arduino.D7_PWM, L298N1.IN1
  N7: Sorting_Arduino.D13_PWM, Part5.CK/TX
  N8: Sorting_Arduino.D12_PWM, Part5.DO/RX
  N9: Sorting_Arduino.D11_PWM, Part4.CK/TX
  N10: Sorting_Arduino.D10_PWM, Part4.DO/RX
  N11: Sorting_Arduino.D9_PWM, Part3.CK/TX
  N12: Sorting_Arduino.D8_PWM, Part3.DO/RX
  GND_2: Sorting_Arduino.GND, Good_Servo_Arm.gnd, Good_Proxy.pin2, Part3.GND, Part4.GND, Part5.GND, Bad_Servo_Arm.gnd, Bad_Proxy.pin2, Defected_Servo_Arm.gnd, Defected_Proxy.pin2
  N13: Sorting_Arduino.D2_PWM, Good_Servo_Arm.pulse
  N14: Sorting_Arduino.D3_PWM, Bad_Servo_Arm.pulse
  N15: Sorting_Arduino.D4_PWM, Defected_Servo_Arm.pulse
  N16: Sorting_Arduino.D22, Good_Proxy.pin1
  N17: Sorting_Arduino.D23, Bad_Proxy.pin1
  N18: Sorting_Arduino.D24, Defected_Proxy.pin1
  VCC: Good_Servo_Arm.vcc, Good_Proxy.pin3, Part3.VCC, Part4.VCC, Part5.VCC, Bad_Servo_Arm.vcc, Bad_Proxy.pin3, Defected_Servo_Arm.vcc, Defected_Proxy.pin3
  N19: BAT1.V+, L298N1.12V
  N20: Conveyor_Motor.pin_1, L298N1.OUT2
  N21: Conveyor_Motor.pin_2, L298N1.OUT1
  N22: Part3.E+, Load_Cell_(1kg)_-_Good.wire1
  N23: Part3.E-, Load_Cell_(1kg)_-_Good.wire3
  N24: Part3.A+, Load_Cell_(1kg)_-_Good.wire2
  N25: Part3.A-, Load_Cell_(1kg)_-_Good.wire4
  N26: SERIAL_COMM_2.usb, USBTTL3.usb
  N27: SERIAL_COMM_1.usb, USBTTL4.usb
  N28: Buffer_Motor.pin_1, L298N1.OUT4
  N29: Buffer_Motor.pin_2, L298N1.OUT3
  N30: L298N1.5V#9, L298N1.ENA
  N31: L298N1.5V#10, L298N1.ENB
  N32: Part4.E+, Load_Cell_(1kg)_-_Bad.wire1
  N33: Part4.E-, Load_Cell_(1kg)_-_Bad.wire3
  N34: Part4.A+, Load_Cell_(1kg)_-_Bad.wire2
  N35: Part4.A-, Load_Cell_(1kg)_-_Bad.wire4
  N36: Part5.E+, Load_Cell_(1kg)_Defected.wire1
  N37: Part5.E-, Load_Cell_(1kg)_Defected.wire3
  N38: Part5.A+, Load_Cell_(1kg)_Defected.wire2
  N39: Part5.A-, Load_Cell_(1kg)_Defected.wire4

custom parts:
  Load Cell - Red/white/black/green: A rectangle load cell/weighting pressure Sensor with four wires - Red, white, black, green. Normally corresponding with E+, E-, A+, A- respectively.
  L298N DC motor driver: 2x DC motor driver with 78M05 positive voltage regulator (7..35 V) L298N: max 46 V, 2 A Set 5 V Enable jumper to enable 5 V regultor (needed for the L298N) and +5 V output at screw terminal or supply external +5 V at screw terminal Set ENA and/or ENB to +5 V to enable motor permanently or supply ENA and/or ENB with PWM signal IN1 and IN2 set rotation directory for motor A (OUT1/OUT2) IN2 and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
